# Fritzing sketch capstone1 (saved by Fritzing 0.9.3b)
breadboards: 1

parts:
  Raspberry_Pi_2 = Raspberry Pi 3 [part_number=RPI-3-V1.2]
  R37 = Resistor [tolerance=±5% resistance=150 package="2010 [SMD]"]
  R27 = Resistor [tolerance=±5% resistance=150 package="2010 [SMD]"]
  C40 = Ceramic Capacitor [capacitance="100 nF" voltage=10V part_number=2a103j package="100 mil [THT, multilayer]"]
  C24 = Ceramic Capacitor [capacitance="100 nF" voltage=10V part_number=2a103j package="100 mil [THT, multilayer]"]
  TRS6 = Audio Jack (TRS) 3.5mm [package="4Ucon 08780 [THT]"]
  C34 = Electrolytic Capacitor [capacitance=10μF package="0605 [SMD, electrolytic]"]
  C32 = Electrolytic Capacitor [capacitance=10μF package="0605 [SMD, electrolytic]"]
  R38 = Resistor [tolerance=±5% resistance=150 package="2010 [SMD]"]
  R32 = Resistor [tolerance=±5% resistance=150 package="2010 [SMD]"]
  R43 = Resistor [tolerance=±5% resistance=150 package="2010 [SMD]"]
  R28 = Resistor [tolerance=±5% resistance=150 package="2010 [SMD]"]
  R45 = Resistor [tolerance=±5% resistance=150 package="2010 [SMD]"]
  R31 = Resistor [tolerance=±5% resistance=150 package="2010 [SMD]"]
  C41 = Ceramic Capacitor [capacitance="100 nF" voltage=10V part_number=2a103j package="100 mil [THT, multilayer]"]
  C36 = Ceramic Capacitor [capacitance="100 nF" voltage=10V part_number=2a103j package="100 mil [THT, multilayer]"]
  C41_2 = Electrolytic Capacitor [capacitance=10μF package="0605 [SMD, electrolytic]"]
  C29 = Electrolytic Capacitor [capacitance=10μF package="0605 [SMD, electrolytic]"]
  TRS9 = Audio Jack (TRS) 3.5mm [package="4Ucon 08780 [THT]"]
  C26 = Electrolytic Capacitor [capacitance=10μF package="0605 [SMD, electrolytic]"]
  TRS11 = Audio Jack (TRS) 3.5mm [package="4Ucon 08780 [THT]"]
  C39 = Ceramic Capacitor [capacitance="100 nF" voltage=10V part_number=2a103j package="100 mil [THT, multilayer]"]
  R29 = Resistor [tolerance=±5% resistance=150 package="2010 [SMD]"]
  R46 = Resistor [tolerance=±5% resistance=150 package="2010 [SMD]"]
  C28 = Electrolytic Capacitor [capacitance=10μF package="0605 [SMD, electrolytic]"]
  C43 = Ceramic Capacitor [capacitance="100 nF" voltage=10V part_number=2a103j package="100 mil [THT, multilayer]"]
  R48 = Resistor [tolerance=±5% resistance=150 package="2010 [SMD]"]
  R49 = Resistor [tolerance=±5% resistance=150 package="2010 [SMD]"]
  C27 = Electrolytic Capacitor [capacitance=10μF package="0605 [SMD, electrolytic]"]
  TRS7 = Audio Jack (TRS) 3.5mm [package="4Ucon 08780 [THT]"]
  C38 = Ceramic Capacitor [capacitance="100 nF" voltage=10V part_number=2a103j package="100 mil [THT, multilayer]"]
  R30 = Resistor [tolerance=±5% resistance=150 package="2010 [SMD]"]
  C33 = Electrolytic Capacitor [capacitance=10μF package="0605 [SMD, electrolytic]"]
  C42 = Ceramic Capacitor [capacitance="100 nF" voltage=10V part_number=2a103j package="100 mil [THT, multilayer]"]
  R42 = Resistor [tolerance=±5% resistance=150 package="2010 [SMD]"]
  R36 = Resistor [tolerance=±5% resistance=150 package="2010 [SMD]"]
  R44 = Resistor [tolerance=±5% resistance=150 package="2010 [SMD]"]
  C31 = Electrolytic Capacitor [capacitance=10μF package="0605 [SMD, electrolytic]"]
  TRS10 = Audio Jack (TRS) 3.5mm [package="4Ucon 08780 [THT]"]
  C37 = Ceramic Capacitor [capacitance="100 nF" voltage=10V part_number=2a103j package="100 mil [THT, multilayer]"]
  R34 = Resistor [tolerance=±5% resistance=150 package="2010 [SMD]"]
  C30 = Electrolytic Capacitor [capacitance=10μF package="0605 [SMD, electrolytic]"]
  C35 = Ceramic Capacitor [capacitance="100 nF" voltage=10V part_number=2a103j package="100 mil [THT, multilayer]"]
  R35 = Resistor [tolerance=±5% resistance=150 package="2010 [SMD]"]
  R40 = Resistor [tolerance=±5% resistance=150 package="2010 [SMD]"]
  R41 = Resistor [tolerance=±5% resistance=150 package="2010 [SMD]"]

nets:
  N1: Raspberry_Pi_2.GIPO27, R38.Pin_0
  N2: Raspberry_Pi_2.GIPO22, R43.Pin_0
  N3: Raspberry_Pi_2.GIPO5, R49.Pin_0
  N4: Raspberry_Pi_2.GIPO6, R42.Pin_0
  N5: Raspberry_Pi_2.GIPO13, R44.Pin_0
  N6: Raspberry_Pi_2.GIPO19, R41.Pin_0
  N7: Raspberry_Pi_2.GIPO26, R40.Pin_0
  GND: Raspberry_Pi_2.GND, R27.Pin_0, C40.0, C24.0, TRS6.Ring, R32.Pin_0, R28.Pin_0, R31.Pin_0, C41.0, C36.0, TRS9.Ring, TRS11.Ring, C39.0, R29.Pin_0, C43.0, R48.Pin_0, TRS7.Ring, C38.0, R30.Pin_0, C42.0, R36.Pin_0, TRS10.Ring, C35.0, R35.Pin_0
  N8: Raspberry_Pi_2.GIPO24, R46.Pin_0
  N9: Raspberry_Pi_2.GIPO23, R45.Pin_0
  N10: Raspberry_Pi_2.GIPO15, R37.Pin_0
  5V: Raspberry_Pi_2.5V
  N11: R37.Pin_1, R27.Pin_1, C34.-
  N12: TRS6.Sleeve, C34.+
  N13: TRS6.Tip, C32.+
  N14: C32.-, R38.Pin_1
  N15: R43.Pin_1, R31.Pin_1, C36.1, C29.-
  N16: R28.Pin_1, R45.Pin_1, C41.1, C41_2.-
  N17: C41_2.+, TRS9.Tip
  N18: C29.+, TRS9.Sleeve
  N19: C26.-, C39.1, R29.Pin_1, R46.Pin_1
  N20: C26.+, TRS11.Sleeve
  N21: TRS11.Tip, C28.+
  N22: C28.-, C43.1, R48.Pin_1, R49.Pin_1
  N23: C27.-, C38.1, R30.Pin_1, R42.Pin_1
  N24: C27.+, TRS7.Sleeve
  N25: TRS7.Tip, C33.+
  N26: C33.-, C42.1, R36.Pin_1, R44.Pin_1
  N27: C31.-, C37.1, R34.Pin_1, R41.Pin_1
  N28: C31.+, TRS10.Sleeve
  N29: TRS10.Tip, C30.+
  N30: C37.0, R34.Pin_0
  N31: C30.-, C35.1, R35.Pin_1, R40.Pin_1
